# Fritzing sketch #SmartPakku (Arduino Uno) (saved by Fritzing 0.9.1b)
circuit board: 5cm x 5.3cm
breadboards: 1
perfboards: 1

parts:
  J1 = Basic Force Sensing Resistor (FSR) [package=THT]
  R2 = Resistor [tolerance=±5% resistance=10k package=THT]
  Part1 = Arduino Uno (Rev3)
  J4 = Basic Force Sensing Resistor (FSR) [package=THT]
  J3 = Basic Force Sensing Resistor (FSR) [package=THT]
  R3 = Resistor [tolerance=±5% resistance=10k package=THT]
  R4 = Resistor [tolerance=±5% resistance=10k package=THT]
  RF1 = nRF8001 Bluetooth LE Breakout
  J5 = Basic Force Sensing Resistor (FSR) [package=THT]
  R5 = Resistor [tolerance=±5% resistance=10k package=THT]

nets:
  N1: J1.pin_0, Part1.A3, R4.Pin_0
  5V: J1.pin_1, Part1.5V, J4.pin_1, J3.pin_1, RF1.VIN, J5.pin_1
  N2: R2.Pin_0, Part1.A1, J4.pin_0
  GND: R2.Pin_1, Part1.GND, R3.Pin_1, R4.Pin_1, RF1.GND, R5.Pin_1
  N3: Part1.A0, J5.pin_0, R5.Pin_0
  N4: Part1.A2, J3.pin_0, R3.Pin_0
  N5: Part1.D9_PWM, RF1.RST
  N6: Part1.D10_PWM/SS, RF1.REQ
  N7: Part1.D11_PWM/MOSI, RF1.MOSI
  N8: Part1.D12/MISO, RF1.MISO
  N9: Part1.D13/SCK, RF1.SCK
  N10: Part1.D2, RF1.RDY

custom parts:
  nRF8001 Bluetooth LE Breakout: nRF8001 Breakout Board
