# Fritzing sketch SmartPakku (Adafruit FLORA) (saved by Fritzing 0.9.1b)
circuit board: 5cm x 5.3cm
breadboards: 1
perfboards: 1

parts:
  J1 = Basic Force Sensing Resistor (FSR) [package=THT]
  R2 = Resistor [tolerance=±5% resistance=10k package=THT]
  J4 = Basic Force Sensing Resistor (FSR) [package=THT]
  J3 = Basic Force Sensing Resistor (FSR) [package=THT]
  R3 = Resistor [tolerance=±5% resistance=10k package=THT]
  R4 = Resistor [tolerance=±5% resistance=10k package=THT]
  RF1 = nRF8001 Bluetooth LE Breakout
  J5 = Basic Force Sensing Resistor (FSR) [package=THT]
  R5 = Resistor [tolerance=±5% resistance=10k package=THT]
  FLORA1 = Adafruit_Flora
  Part1 = Power Cell LiPo Charger/Booster
  BATT1 = LiPoly Battery (1300mAh)

nets:
  N1: J1.pin_0, R4.Pin_0, FLORA1.connector13
  N2: J1.pin_1, J4.pin_1, J3.pin_1, RF1.VIN, J5.pin_1, FLORA1.connector14
  N3: R2.Pin_0, J4.pin_0, FLORA1.connector10
  N4: R2.Pin_1, R3.Pin_1, R4.Pin_1, R5.Pin_1, FLORA1.connector1
  N5: J3.pin_0, R3.Pin_0, FLORA1.connector12
  N6: RF1.GND, FLORA1.connector11
  N7: J5.pin_0, R5.Pin_0, FLORA1.connector9
  N8: FLORA1.connector2, Part1.PS
  N9: FLORA1.connector3, Part1.EN
  N10: Part1.VCC, BATT1.positive
  N11: Part1.GND, BATT1.negative

custom parts:
  nRF8001 Bluetooth LE Breakout: nRF8001 Breakout Board
  LiPoly Battery (1300mAh): Lithium Ion Polymer Battery (1300mAh)
